# Fritzing sketch theremin (saved by Fritzing 0.9.2b)
breadboards: 1

parts:
  Parte1 = Arduino Uno (Rev3)
  J1 = Piezo Speaker
  R1 = Resistor [tolerance=±5% resistance=100k package=THT]
  R2 = Photocell (LDR) [package=THT]

nets:
  N1: Parte1.A5/SCL, R1.Pin_1, R2.pin_1
  N2: Parte1.GND, J1.pin1, R1.Pin_0
  N3: Parte1.D5_PWM, J1.pin2
  N4: Parte1.5V, R2.pin_0
