# Fritzing sketch uselessbox (saved by Fritzing 0.9.2b)
breadboards: 1

parts:
  Parte1 = Arduino Uno (Rev3) - ICSP
  U3 = SWITCH_SPDT [package=kps-1290]
  J1 = Basic Servo

nets:
  N1: Parte1.D8, U3.S
  N2: Parte1.D9_PWM, U3.P
  N3: Parte1.D10_PWM/SS, J1.pulse
  5V: Parte1.5V, J1.vcc
  GND: Parte1.GND, U3.O, J1.gnd
